# Fritzing sketch 1_GPIO_DigitalRead (saved by Fritzing 0.9.2b)
breadboards: 1

parts:
  Part1 = Intel Edison Arduinobreakout
  S1 = Pushbutton [package="[THT]"]

nets:
  N1: Part1.D6_PWM, S1.Pin_1, S1.Pin_2
  N2: Part1.GND, S1.Pin_3, S1.Pin_4
