# Fritzing sketch 2_AioA0 (saved by Fritzing 0.9.2b)

parts:
  Part1 = Intel Edison Arduinobreakout
  R1 = Rotary Potentiometer (Small) [maximum_resistance=100kΩ package=THT]

nets:
  N1: Part1.A0, R1.wiper
  N2: Part1.5V, R1.leg2
  N3: Part1.GND, R1.leg1
