# Fritzing sketch 3_Isr (saved by Fritzing 0.9.2b)
breadboards: 1

parts:
  Part1 = Intel Edison Arduinobreakout
  S1 = Pushbutton [package="[THT]"]
  S2 = Pushbutton [package="[THT]"]

nets:
  N1: Part1.GND, S1.Pin_1, S1.Pin_2, S2.Pin_1, S2.Pin_2
  N2: Part1.D6_PWM, S2.Pin_3, S2.Pin_4
  N3: Part1.D7, S1.Pin_3, S1.Pin_4
