# Fritzing sketch 3_IsrRotatryEncoder (saved by Fritzing 0.9.2b)

parts:
  Part1 = Intel Edison Arduinobreakout
  RE1 = Rotary Encoder [package=THT]

nets:
  N1: Part1.D6_PWM, RE1.EncoderPinA
  N2: Part1.D7, RE1.EncoderPinB
  N3: Part1.GND, RE1.EncoderPinC
