# Fritzing sketch 4_WebGuiTest (saved by Fritzing 0.9.2b)
breadboards: 1

parts:
  Part1 = Intel Edison Arduinobreakout
  S1 = Pushbutton [package="[THT]"]
  S2 = Pushbutton [package="[THT]"]
  R1 = Rotary Potentiometer (Small) [maximum_resistance=100kΩ package=THT]
  S3 = Pushbutton [package="[THT]"]

nets:
  N1: Part1.A0, R1.wiper
  N2: Part1.GND, S1.Pin_1, S1.Pin_2, S2.Pin_1, S2.Pin_2, R1.leg2, S3.Pin_1, S3.Pin_2
  N3: Part1.D5_PWM, S1.Pin_3, S1.Pin_4
  N4: Part1.D6_PWM, S2.Pin_3, S2.Pin_4
  N5: Part1.D7, S3.Pin_3, S3.Pin_4
  N6: Part1.5V, R1.leg1
